# Fritzing sketch circuit (saved by Fritzing 0.9.5d)
circuit board: 10cm x 10cm
breadboards: 3

parts:
  Part2 = Adafruit CCS811
  Part3 = Adafruit ADS1115 16Bit I2C ADC [part_number="Adafruit #1085"]
  Part4 = Adafruit ADS1115 16Bit I2C ADC [part_number="Adafruit #1085"]
  Part5 = Adafruit SHT31-D Sensirion Temperature/Humidity Sensor [part_number="Adafruit #2857"]
  Part6 = Adafruit BMP388 - Barometric Pressure and Altimeter [part_number="Adafruit #3966"]
  Part7 = Adafruit Feather M4 Express [part_number="Adafruit #3857"]
  U3 = mystery part, 2 pins [chip_label=FAN]
  U2 = mystery part, 12 pins [chip_label=Alphasense]
  U4 = mystery part, 5 pins [chip_label=D36V28F5]
  U5 = mystery part, 2 pins [chip_label=BATT]
  JP1 = Header 12 [package=1x12_machine-pin-header_lock.004]
  JP2 = M16 [package=1x16_machine-pin-header_lock.004]
  JP4 = M16 [package=1x16_machine-pin-header_lock.004]
  JP3 = M16 [package=1x16_machine-pin-header_lock.004]
  Part9 = Arduino Nano (Rev3.0)
  U6 = mystery part, 8 pins [chip_label=PMS5003]
  U8 = mystery part, 5 pins [chip_label=D36V28F3]
  S1 = SPST Switch [package=switch-spdt]
  S2 = SPST Switch [package=switch-spdt]
  R1 = Resistor [tolerance=±5% resistance=10k package=THT]
  Q1 = MOSFET-NCHANNEL [package=to220v]

nets (from the breadboard view):
  VIN: Part2.VIN, Part3.VDD, Part4.ADDR, Part4.VDD, Part5.VIN, Part6.VIN, Part7.+3V3, JP4.2, JP3.2, Part9.3V3, U8.pin1, S2.S
  GND: Part2.GND, Part2.!WAKE, Part3.ADDR, Part3.GND, Part4.GND, Part5.GND, Part6.GND, Part7.GND, U2.pin2, U4.pin2, U4.pin3, U5.pin2, JP2.12, JP4.4, JP3.14, Part9.GND, U6.pin2, U8.pin2, U8.pin3, S1.P, R1.Pin_1, Q1.S
  N1: Part2.SDA, Part3.SDA, Part4.SDA, Part5.SDA, Part6.SDI/SDA, Part7.SDA, JP1.12
  N2: Part2.SCL, Part3.SCL, Part4.SCL, Part5.SCL, Part6.SCK/SCL, Part7.SCL, JP1.11
  N3: Part3.AIN3, U2.pin9
  N4: Part3.AIN2, U2.pin4
  N5: Part3.AIN1, U2.pin8
  N6: Part3.AIN0, U2.pin5
  N7: Part4.AIN3, U2.pin12
  N8: Part4.AIN2, U2.pin1
  N9: Part4.AIN1, U2.pin10
  N10: Part4.AIN0, U2.pin3
  N11: Part7.D4, JP4.16, Q1.G
  N12: Part7.TX_D1, JP4.15
  N13: Part7.RX_D0, JP4.14
  N14: Part7.MISO, JP4.13
  N15: Part7.MOSI, JP4.12
  N16: Part7.SCK, JP4.11
  N17: Part7.A5, JP4.10, S2.P
  N18: Part7.A4, JP2.9, JP4.9, Part9.D4
  N19: Part7.A3, JP4.8
  N20: Part7.A2, JP4.7
  N21: Part7.A1, JP4.6
  N22: Part7.A0, JP4.5
  N23: Part7.AREF, JP4.3
  N24: Part7.!RESET, JP4.1
  N25: Part7.VBAT, JP1.1
  N26: Part7.EN, JP1.2
  N27: Part7.VBUS, JP1.3
  N28: Part7.D13, JP1.4, JP2.15, Part9.D1/TX
  N29: Part7.D12, JP1.5, JP2.14, Part9.D0/RX
  N30: Part7.D11, JP1.6
  N31: Part7.D10, JP1.7
  N32: Part7.D9, JP1.8
  N33: Part7.D6, JP1.9
  N34: Part7.D5, JP1.10
  N35: U3.pin1, U4.pin4, U5.pin1, U8.pin4
  N36: U3.pin2, Q1.D
  N37: U2.pin11, U4.pin1, JP3.12, Part9.5V, U6.pin1
  N38: U4.pin5, U8.pin5, S1.O
  N39: JP2.1, Part9.D12/MISO
  N40: JP2.2, Part9.D11/MOSI
  N41: JP2.3, Part9.D10
  N42: JP2.4, Part9.D9
  N43: JP2.5, Part9.D8
  N44: JP2.6, Part9.D7
  N45: JP2.7, Part9.D6
  N46: JP2.8, Part9.D5
  N47: JP2.10, Part9.D3, U6.pin4
  N48: JP2.11, Part9.D2, U6.pin5
  N49: JP2.13, JP3.13, Part9.RESET
  N50: JP3.1, Part9.D13/SCK
  N51: JP3.3, Part9.AREF
  N52: JP3.4, Part9.A0
  N53: JP3.5, Part9.A1
  N54: JP3.6, Part9.A2
  N55: JP3.7, Part9.A3
  N56: JP3.8, Part9.A4
  N57: JP3.9, Part9.A5
  N58: JP3.10, Part9.A6
  N59: JP3.11, Part9.A7
  N60: JP3.15, Part9.VIN
  N61: S2.O, R1.Pin_0

notes:
  +9V
  ELACYC
  PCB V2
  on
  off
  10K
  log
  run
  stop
  power
  fan
  GND
  notch +V
  CCS811
  BMP388
  ADS1115 0x49
  ADS1115 0x48
  SHT31

custom parts:
  Adafruit ADS1115 16Bit I2C ADC: For microcontrollers without an analog-to-digital converter or when you want a higher-precision ADC, the ADS1115 provides 16-bit precision at 860 samples/second over I2C. The chip can be configured as 4 single-ended input channels, or two differential channels. As a nice bonus, it even includes a programmable gain amplifier, up to x16, to help boost up smaller single/differential signals to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
  Adafruit SHT31-D Sensirion Temperature/Humidity Sensor: Sensirion Temperature/Humidity sensors are some of the finest & highest-accuracy devices you can get. And, finally we have some that have a true I2C interface for easy reading. The SHT31-D sensor has an excellent ±2% relative humidity and ±0.3°C accuracy for most uses. Unlike earlier SHT sensors, this sensor has a true I2C interface, and (bonus!) even with two address options. It also is 3V or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
  Adafruit Feather M4 Express: It's what you've been waiting for, the Feather M4 Express featuring ATSAMD51. This Feather is fast like a swift, smart like an owl, strong like a ox-bird (it's half ox, half bird, OK?) This feather is powered by our new favorite chip, the ATSAMD51J19 - with its 120MHz Cortex M4 with floating point support and 512KB Flash and 192KB RAM. Your code will zig and zag and zoom, and with a bunch of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
